# Fritzing sketch InfoCheck (saved by Fritzing 0.7.10b)
breadboards: 1

parts:
  R1 = Rotary Potentiometer (Small) [maximum_resistance=10kΩ]
  LCD1 = LCD screen
  Pi1 = Adafruit Pi Cobbler

nets (from the breadboard view):
  VSS: R1.leg1, LCD1.VSS, LCD1.R/W, LCD1.LED-, Pi1.GND
  N1: R1.wiper, LCD1.V0
  N2: R1.leg2, LCD1.VDD, LCD1.LED+, Pi1.5V0
  N3: LCD1.RS, Pi1.#25
  N4: LCD1.E, Pi1.#24
  N5: LCD1.DB4, Pi1.#23
  N6: LCD1.DB5, Pi1.#17
  N7: LCD1.DB6, Pi1.#21
  N8: LCD1.DB7, Pi1.#22

custom parts:
  Adafruit Pi Cobbler: Adafruit Pi Cobbler GPIO Breakout for Raspberry Pi
